# Fritzing sketch Cable_Schema_Sharon (saved by Fritzing 0.9.3b)
breadboards: 1

parts:
  U1 = NodeMCU V1.0
  Componente1 = Rotoshield - Motor driver shield for Arduino
  hc-sr1 = hc-sr04
  S1 = Pololu QTR-8 Reflectabce Sensor array [package=THT]
  S2 = Pololu QTR-8 Reflectabce Sensor array [package=THT]
  M1 = DC Motor
  M2 = DC Motor
  M3 = DC Motor
  M4 = DC Motor

nets:
  N1: U1.D0, Componente1.DIG_0
  N2: U1.D1, Componente1.DIG_1
  N3: U1.D2, Componente1.DIG_2
  N4: U1.D3, hc-sr1.Echo
  N5: U1.D4, hc-sr1.Trig
  3V3: U1.3V3, Componente1.VIN
  GND: U1.GND, Componente1.GND, hc-sr1.GND, S1.pin1, S1.pin21, S2.pin1, S2.pin15, S2.pin19, M1.pin_2, M2.pin_2, M3.pin_1, M4.pin_1
  N6: U1.D5, Componente1.DIG_5
  N7: U1.D6, Componente1.DIG_6
  N8: U1.D7, Componente1.DIG_7
  N9: U1.D8, S2.pin3, S2.pin5
  N10: U1.RX, S1.pin3, S1.pin5
  VCC: U1.RSV, Componente1.VCC, hc-sr1.VCC, S1.pin2, S1.pin22, S2.pin2, S2.pin14
  N11: Componente1.+5V, M1.pin_1, M2.pin_1, M3.pin_2, M4.pin_2

notes:
  GRD
  VCC
  WARNIG:
  this is not the real Double H-bridge
  mounted on the car, because we couldn't find the same model for this Fritzing sketch
  ^
  ADDITIONAL 5V alimentation for the motor
  LINE TRACING SENSOR

custom parts:
  NodeMCU V1.0: ESP8266 based NodeMCU
